# Fritzing sketch A01 (saved by Fritzing 0.9.3b)
breadboards: 1

parts:
  R1 = Resistor [tolerance=±5% resistance=220 package=THT]
  R2 = Resistor [tolerance=±5% resistance=220 package=THT]
  LED1 = smd LED [color="Red (660nm)" package="0805 [SMD]"]
  LED2 = smd LED [color="Red (660nm)" package="0805 [SMD]"]
  Part1 = Arduino Mega 2560 (Rev3)
  SW1 = DIP Switch 8 Position [package=dipswitch-08]
  R3 = Resistor [tolerance=±5% resistance=220 package=THT]
  R4 = Resistor [tolerance=±5% resistance=220 package=THT]
  R5 = Resistor [tolerance=±5% resistance=220 package=THT]
  R7 = Resistor [tolerance=±5% resistance=220 package=THT]
  R9 = Resistor [tolerance=±5% resistance=220 package=THT]
  R10 = Resistor [tolerance=±5% resistance=220 package=THT]
  R11 = Resistor [tolerance=±5% resistance=220 package=THT]
  R12 = Resistor [tolerance=±5% resistance=220 package=THT]
  LED4 = RGB LED (com. cathode, rbg) [package="5 mm [THT]"]
  LED5 = RGB LED (com. cathode, rbg) [package="5 mm [THT]"]

nets:
  N1: R1.Pin_0, LED1.cathode
  N2: R1.Pin_1, R2.Pin_1, Part1.GND, R9.Pin_1, R10.Pin_1, LED4.common_cathode, LED5.common_cathode
  N3: R2.Pin_0, LED2.cathode
  N4: LED1.anode, Part1.D53
  N5: LED2.anode, Part1.D52
  N6: Part1.D11_PWM, SW1.16, R10.Pin_0
  N7: Part1.D10_PWM, SW1.15, R9.Pin_0
  N8: Part1.5V, SW1.1, SW1.2
  N9: Part1.D2_PWM, R3.Pin_0
  N10: Part1.D3_PWM, R4.Pin_0
  N11: Part1.D4_PWM, R5.Pin_0
  N12: Part1.D5_PWM, R7.Pin_0
  N13: Part1.D6_PWM, R11.Pin_0
  N14: Part1.D7_PWM, R12.Pin_0
  N15: R3.Pin_1, LED4.red_anode
  N16: R4.Pin_1, LED4.blue_anode
  N17: R5.Pin_1, LED4.green_anode
  N18: R7.Pin_1, LED5.red_anode
  N19: R11.Pin_1, LED5.blue_anode
  N20: R12.Pin_1, LED5.green_anode
