# Fritzing sketch A02 (saved by Fritzing 0.9.3b)
breadboards: 1

parts:
  Part1 = Arduino Mega 2560 (Rev3)
  LED1 = smd LED [color="Yellow (595nm)" package="0603 [SMD]"]
  LED2 = smd LED [color="Red (633nm)" package="0603 [SMD]"]
  LED3 = smd LED [color="Green (555nm)" package="0603 [SMD]"]
  R1 = Resistor [tolerance=±5% resistance=220 package="0402 [SMD]"]
  S1 = Round Pushbutton
  R2 = PHOTOCELL [package=photocell]
  R3 = Resistor [tolerance=±5% resistance=220 package="0402 [SMD]"]
  T1 = TMP36 Temperature Sensor [package="TO92 [THT]"]
  U1 = POT [package=pot_alpha_rv16af-20]
  R4 = Resistor [tolerance=±5% resistance=220 package="0402 [SMD]"]

nets:
  N1: Part1.A0, U1.S
  N2: Part1.A1, R2.P$2, R3.Pin_1
  N3: Part1.A2, T1.Vout
  N4: Part1.D12_PWM, R1.Pin_1, S1.leg0
  N5: Part1.5V, S1.leg1, R2.P$1, T1.+Vs, U1.A
  GND: Part1.GND, R1.Pin_0, R3.Pin_0, T1.GND, U1.E, R4.Pin_1
  N6: Part1.D2_PWM, LED3.anode
  N7: Part1.D3_PWM, LED1.anode
  N8: Part1.D4_PWM, LED2.anode
  N9: LED1.cathode, LED2.cathode, LED3.cathode, R4.Pin_0
