# Fritzing sketch Part1 (saved by Fritzing 0.9.3b)
breadboards: 1

parts:
  R1 = Resistor [tolerance=±5% resistance=220 package=THT]
  R2 = Resistor [tolerance=±5% resistance=220 package=THT]
  LED1 = LED - 5mm [color="Green (555nm)" package="5 mm [THT]"]
  LED2 = LED - 5mm [color="Red (633nm)" package="5 mm [THT]"]
  Part1 = Arduino Mega ADK (Rev3)
  S1 = Round Pushbutton

nets:
  N1: R1.Pin_0, LED1.cathode
  N2: R1.Pin_1, R2.Pin_1, Part1.GND, S1.leg1
  N3: R2.Pin_0, LED2.cathode
  N4: LED1.anode, Part1.D2_PWM
  N5: LED2.anode, Part1.D3_PWM
  N6: Part1.D4_PWM, S1.leg0
