# Fritzing sketch p2 (saved by Fritzing 0.9.3b)
breadboards: 1

parts:
  U1 = TMP36 [package=to-92]
  Part1 = Arduino Mega ADK (Rev3)
  U2 = LCD-16X2 [package=lcd-16x2]

nets:
  VCC: U1.VCC, Part1.5V, U2.VDD
  N1: U1.VOUT, Part1.A5
  GND: U1.GND, Part1.GND, U2.VSS
  N2: Part1.D2_PWM, U2.VO
