# Fritzing sketch p6 (saved by Fritzing 0.9.3b)
breadboards: 1

parts:
  R3 = Resistor [tolerance=±5% resistance=220 package=THT]
  R4 = PHOTOCELL [package=photocell]
  Part1 = Arduino Mega 2560 (Rev3)
  U1 = TMP36 [package=to-92-kit]
  R5 = Resistor [tolerance=±5% resistance=220 package=THT]

nets:
  N1: R3.Pin_0, R4.P$1, Part1.A2
  N2: R3.Pin_1, Part1.GND, R5.Pin_1
  5V: R4.P$2, Part1.5V, U1.VCC
  N3: Part1.A3, U1.VOUT
  N4: U1.GND, R5.Pin_0
